# Fritzing sketch Example wiring - 2 pots, 3 buttons (saved by Fritzing 0.9.3b)

parts:
  Part1 = Arduino Micro (Rev3)
  U1 = POT [package=pot_alpha_rv16af-20]
  U2 = POT [package=pot_alpha_rv16af-20]
  S1 = Round Pushbutton
  S2 = Round Pushbutton
  S3 = Round Pushbutton
  LED1 = LED - 3mm [color="Red (633nm)" package="3 mm [THT]"]
  LED2 = LED - 3mm [color="Red (633nm)" package="3 mm [THT]"]
  LED3 = LED - 3mm [color="Red (633nm)" package="3 mm [THT]"]
  R1 = Resistor [tolerance=±5% resistance=220 package="2512 [SMD]"]
  R2 = Resistor [tolerance=±5% resistance=220 package="2512 [SMD]"]
  R3 = Resistor [tolerance=±5% resistance=220 package="2512 [SMD]"]
  C1 = Capacitor Polarized [package=panasonic_e]
  C2 = Capacitor Polarized [package=panasonic_e]

nets:
  N1: Part1.D3/SCL, LED1.cathode
  N2: Part1.D5_PWM, LED2.cathode
  N3: Part1.D6_PWM/A7, LED3.cathode
  N4: Part1.D7, S1.leg1
  N5: Part1.D8_PWM/A8, S2.leg1
  N6: Part1.D9_PWM/A9, S3.leg1
  N7: Part1.GND, U1.A, U2.A, S1.leg0, S2.leg0, S3.leg0, C1.-, C2.-
  N8: Part1.5V, U1.E, U2.E, R1.Pin_1, R2.Pin_1, R3.Pin_1
  N9: Part1.A1, U2.S, C1.+
  N10: Part1.A0, U1.S, C2.+
  N11: LED1.anode, R1.Pin_0
  N12: LED2.anode, R2.Pin_0
  N13: LED3.anode, R3.Pin_0
